// Digital circuit circuito_completo.dig as structural Verilog
module circuito_completo (
  input  di,
  input  ni,
  input  qi,
  input  C,
  output co,
  output \do ,
  output no
);

  wire A, and_1_out, and_2_out, and_3_out, and_4_out, and_5_out, and_6_out, and_7_out, and_8_out, and_9_out,
       and_10_out, and_11_out, and_12_out, and_13_out, and_14_out, and_15_out, and_16_out, and_17_out,
       and_18_out, and_19_out, and_20_out, and_21_out, and_22_out, and_23_out, and_24_out, and_25_out,
       and_26_out, and_27_out, and_28_out, and_29_out, and_30_out, and_31_out, and_32_out, and_33_out,
       and_34_out, and_35_out, and_36_out, and_37_out, and_38_out, and_39_out, B, C_t, D, not_1_out,
       not_2_out, not_3_out, not_4_out, not_5_out, not_6_out, not_7_out, not_8_out, not_9_out, not_10_out,
       not_11_out, not_12_out, or_1_out, or_2_out, or_3_out, or_7_out, or_8_out, or_9_out, Z_0_n, Z_1_n,
       Z_2_n;

  not not_1 (not_1_out, di);
  not not_2 (not_2_out, ni);
  not not_3 (not_3_out, qi);
  not not_4 (not_4_out, Z_2_n);
  not not_5 (not_5_out, Z_1_n);
  not not_6 (not_6_out, Z_0_n);
  and and_1 (and_1_out, not_6_out, not_5_out, not_4_out, not_1_out, not_2_out, qi);
  and and_2 (and_2_out, Z_1_n, qi);
  and and_3 (and_3_out, Z_1_n, ni);
  and and_4 (and_4_out, di, not_2_out, not_3_out);
  and and_5 (and_5_out, not_6_out, not_5_out, not_4_out, not_1_out, ni, not_3_out);
  and and_6 (and_6_out, not_6_out, not_5_out, not_4_out, di, not_2_out, not_3_out);
  and and_7 (and_7_out, Z_0_n, Z_1_n);
  and and_8 (and_8_out, Z_0_n, not_5_out);
  or or_1 (or_1_out, Z_0_n, and_2_out, and_3_out, Z_2_n, and_4_out);
  or or_2 (or_2_out, and_5_out, and_6_out);
  D_FF u_Z_2_n (.D(and_1_out), .C(C), .Q(Z_2_n));  // open: nQ
  D_FF u_Z_1_n (.D(or_1_out), .C(C), .Q(Z_1_n));  // open: nQ
  D_FF u_Z_0_n (.D(or_2_out), .C(C), .Q(Z_0_n));  // open: nQ
  not not_7 (not_7_out, and_7_out);
  not not_8 (not_8_out, and_8_out);
  not not_9 (not_9_out, Z_2_n);
  not not_10 (not_10_out, B);
  not not_11 (not_11_out, C_t);
  not not_12 (not_12_out, D);
  and and_9 (and_9_out, D, C_t, not_10_out, not_7_out, not_8_out, Z_2_n);
  and and_10 (and_10_out, not_12_out, not_11_out, B, not_7_out, not_8_out, Z_2_n);
  and and_11 (and_11_out, D, C_t, not_10_out, not_7_out, and_8_out, not_9_out);
  and and_12 (and_12_out, not_12_out, not_10_out, not_7_out, not_8_out, Z_2_n);
  and and_13 (and_13_out, not_12_out, not_11_out, B, not_9_out);
  and and_14 (and_14_out, not_12_out, not_11_out, B, and_8_out);
  and and_15 (and_15_out, not_12_out, not_11_out, B, and_7_out);
  and and_16 (and_16_out, not_11_out, not_10_out, not_7_out, not_8_out, Z_2_n);
  and and_17 (and_17_out, C_t, not_10_out, and_7_out, not_8_out, not_9_out);
  and and_18 (and_18_out, D, not_11_out, not_10_out, not_7_out, not_8_out, Z_2_n);
  and and_19 (and_19_out, D, not_11_out, not_10_out, not_7_out, and_8_out, not_9_out);
  and and_20 (and_20_out, not_12_out, not_11_out, and_7_out, not_8_out, not_9_out);
  and and_21 (and_21_out, not_12_out, C_t, not_10_out, not_7_out);
  and and_22 (and_22_out, not_11_out, not_10_out, and_7_out, not_8_out, not_9_out);
  and and_23 (and_23_out, C_t, not_10_out, not_7_out, not_8_out, not_9_out);
  and and_24 (and_24_out, C_t, not_10_out, and_8_out, Z_2_n);
  and and_25 (and_25_out, C_t, not_10_out, and_7_out, Z_2_n);
  and and_26 (and_26_out, C_t, not_10_out, and_7_out, and_8_out);
  and and_27 (and_27_out, not_12_out, not_11_out, not_7_out, not_8_out, Z_2_n);
  and and_28 (and_28_out, not_12_out, not_11_out, not_7_out, and_8_out, not_9_out);
  and and_29 (and_29_out, not_12_out, not_10_out, not_7_out, not_8_out, Z_2_n);
  and and_30 (and_30_out, not_12_out, not_10_out, not_7_out, and_8_out, not_9_out);
  and and_31 (and_31_out, D, not_10_out, not_8_out, not_9_out);
  and and_32 (and_32_out, D, not_10_out, and_8_out, Z_2_n);
  and and_33 (and_33_out, D, not_10_out, and_7_out);
  and and_34 (and_34_out, D, B);
  and and_35 (and_35_out, C_t, B);
  and and_36 (and_36_out, D, C_t, B);
  and and_37 (and_37_out, D, A);
  and and_38 (and_38_out, not_12_out, C_t, B);
  and and_39 (and_39_out, not_12_out, A);
  or or_3 (or_3_out, and_9_out, and_10_out);
  or or_4 (co, and_34_out, and_35_out);
  or or_5 (\do , and_36_out, and_37_out);
  or or_6 (no, and_38_out, and_39_out);
  or or_7 (or_7_out, and_11_out, and_12_out, and_13_out, and_14_out, and_15_out, and_16_out, and_17_out, A);
  or or_8 (or_8_out, and_18_out, and_19_out, and_20_out, and_21_out, and_22_out, and_23_out, and_24_out, and_25_out, and_26_out, A);
  or or_9 (or_9_out, and_27_out, and_28_out, and_29_out, and_30_out, and_31_out, and_32_out, and_33_out, A);
  D_FF u_A (.D(or_3_out), .C(C), .Q(A));  // open: nQ
  D_FF u_B (.D(or_7_out), .C(C), .Q(B));  // open: nQ
  D_FF u_C (.D(or_8_out), .C(C), .Q(C_t));  // open: nQ
  D_FF u_D (.D(or_9_out), .C(C), .Q(D));  // open: nQ

  // Notes on the sheet:
  //   C: Hz: 2
endmodule
